# Fritzing sketch circuito (saved by Fritzing 0.4.3b)
breadboards: 1

parts:
  Arduino1 = Arduino  # not connected
  R1 = Photocell (LDR) [package=THT]
  R2 = Photocell (LDR) [package=THT]  # not connected
  LED1 = Red LED - 5mm  # not connected
  R3 = Resistor [resistance=220 package=THT]

nets:
  N1: R1.pin_0, R3.Pin_1
